// Logisim project bcd_7segment.circ as structural Verilog: 2 circuits, main circuit main
module main (
  input  W,
  input  X,
  input  Y,
  input  Z,
  output W_prime_X_prime_Y_prime_Z,
  output A,
  output XY_prime_Z_prime,
  output B,
  output XY_prime_Z,
  output XYZ_prime,
  output C,
  output XYZ,
  output D,
  output XY_prime,
  output X_prime_Y,
  output E,
  output YZ,
  output F,
  output W_prime_X_prime_Z,
  output W_prime_X_prime_Y_prime,
  output G
);

  wire not_1_out, not_2_out, not_3_out, not_4_out;

  not not_1 (not_1_out, W);
  not not_2 (not_2_out, X);
  not not_3 (not_3_out, Y);
  not not_4 (not_4_out, Z);
  and and_1 (W_prime_X_prime_Y_prime_Z, not_1_out, not_2_out, not_3_out, Z);
  and and_2 (XY_prime_Z_prime, X, not_3_out, not_4_out);
  and and_3 (XY_prime_Z, X, not_3_out, Z);
  and and_4 (XYZ_prime, X, Y, not_4_out);
  and and_5 (XYZ, X, Y, Z);
  and and_6 (XY_prime, X, not_3_out);
  and and_7 (X_prime_Y, not_2_out, Y);
  and and_8 (YZ, Y, Z);
  and and_9 (W_prime_X_prime_Z, not_1_out, not_2_out, Z);
  and and_10 (W_prime_X_prime_Y_prime, not_1_out, not_2_out, not_3_out);
  or or_1 (A, W_prime_X_prime_Y_prime_Z, XY_prime_Z_prime);
  or or_2 (B, XY_prime_Z, XYZ_prime);
  and and_11 (C, not_2_out, Y, not_4_out);
  or or_3 (D, W_prime_X_prime_Y_prime_Z, XY_prime_Z_prime, XYZ);
  or or_4 (E, XY_prime, Z);
  or or_5 (F, X_prime_Y, YZ, W_prime_X_prime_Z);
  or or_6 (G, W_prime_X_prime_Y_prime, XYZ);
  _7_Segment_Display #(.active("false")) u_7_segment_display_1 (
    .g(G), .f(F), .a(A), .b(B), .e(E), .d(D), .c(C));  // open: dp

  // Notes on the sheet:
  //   BCD to 7-Segment Decoder | Logisim design
endmodule

module BCD_to_7_Segment (
  input  W,
  input  X,
  input  Y,
  input  Z,
  output A,
  output B,
  output C,
  output D,
  output E,
  output F,
  output G
);

  wire and_1_out, and_2_out, and_4_out, and_5_out, and_6_out, and_7_out, and_8_out, and_9_out, and_10_out,
       and_11_out, and_12_out, and_13_out, and_14_out, not_1_out, not_2_out, not_3_out, not_4_out, not_5_out,
       not_6_out, not_7_out, not_8_out, not_9_out, not_10_out, not_11_out, not_12_out, not_13_out,
       not_14_out, not_15_out, not_16_out, not_17_out, not_18_out, not_19_out, not_20_out, not_21_out;

  not not_1 (not_1_out, W);
  not not_2 (not_2_out, X);
  not not_3 (not_3_out, Y);
  not not_4 (not_4_out, Y);
  not not_5 (not_5_out, Z);
  and and_1 (and_1_out, X, not_6_out, Z);
  not not_6 (not_6_out, Y);
  and and_2 (and_2_out, X, Y, not_7_out);
  not not_7 (not_7_out, Z);
  not not_8 (not_8_out, X);
  and and_3 (C, not_8_out, Y, not_9_out);
  not not_9 (not_9_out, Z);
  not not_10 (not_10_out, W);
  not not_11 (not_11_out, X);
  not not_12 (not_12_out, Y);
  not not_13 (not_13_out, Y);
  not not_14 (not_14_out, Z);
  and and_4 (and_4_out, X, not_15_out);
  not not_15 (not_15_out, Y);
  not not_16 (not_16_out, W);
  not not_17 (not_17_out, X);
  and and_5 (and_5_out, not_16_out, not_17_out, Z);
  not not_18 (not_18_out, X);
  and and_6 (and_6_out, not_18_out, Y);
  and and_7 (and_7_out, Y, Z);
  not not_19 (not_19_out, W);
  not not_20 (not_20_out, X);
  and and_8 (and_8_out, not_19_out, not_20_out, not_21_out);
  not not_21 (not_21_out, Y);
  and and_9 (and_9_out, X, Y, Z);
  and and_10 (and_10_out, not_1_out, not_2_out, not_3_out, Z);
  or or_1 (A, and_10_out, and_11_out);
  and and_11 (and_11_out, X, not_4_out, not_5_out);
  or or_2 (B, and_1_out, and_2_out);
  and and_12 (and_12_out, not_10_out, not_11_out, not_12_out, Z);
  or or_3 (D, and_12_out, and_13_out, and_14_out);
  and and_13 (and_13_out, X, not_13_out, not_14_out);
  and and_14 (and_14_out, X, Y, Z);
  or or_4 (E, Z, and_4_out);
  or or_5 (F, and_5_out, and_6_out, and_7_out);
  or or_6 (G, and_8_out, and_9_out);
endmodule
